# Fritzing sketch Stepper (saved by Fritzing 0.9.3b)
breadboards: 1

parts:
  Part1 = Arduino Nano (Rev3.0) (ICSP)
  M1 = Stepper Motor - Bipolar
  DRV_1 = DRV 8825 Stepper Motor Carrier, High Current [part_number="DRV 8825"]

nets:
  N1: Part1.GND, DRV_1.GROUND_LOG
  N2: Part1.D8, DRV_1.STEP
  N3: Part1.D9, DRV_1.MS3
  N4: Part1.D10, DRV_1.MS2
  N5: Part1.D11/MOSI, DRV_1.MS1
  N6: Part1.5V, DRV_1.VOLTAGE_DD
  N7: M1.A, DRV_1.OUT_2B
  N8: M1.C, DRV_1.OUT_1A
  N9: M1.B, DRV_1.OUT_2A
  N10: M1.D, DRV_1.OUT_1B
