# Fritzing sketch Thermistor (saved by Fritzing 0.9.3b)
breadboards: 1

parts:
  Part1 = Arduino Nano (Rev3.0) (ICSP)
  R1 = Temperature Sensor (Thermistor) [thermistor_type=NTC package=THT]
  R4 = Resistor [tolerance=±5% resistance=220 package="2010 [SMD]"]

nets:
  N1: Part1.GND, R4.Pin_0
  N2: Part1.5V, R1.pin_1
  N3: Part1.A0, R1.pin_0, R4.Pin_1
