# Fritzing sketch Thermistor_Display_tilt (saved by Fritzing 0.9.3b)
breadboards: 1

parts:
  Part1 = Arduino Nano (Rev3.0)
  Grove1 = Grove OLED 128x96
  R5 = Temperature Sensor (Thermistor) [thermistor_type=NTC package=THT]
  R6 = Resistor [tolerance=±5% resistance=220 package="2010 [SMD]"]
  S1 = Tilt Switch [package=THT]

nets:
  GND: Part1.GND, Grove1.GND, R6.Pin_0, S1.Pin_2
  N1: Part1.D2, S1.Pin_1
  5V: Part1.5V, Grove1.VCC, R5.pin_1
  N2: Part1.A5, Grove1.SCL
  N3: Part1.A4, Grove1.SDA
  N4: Part1.A0, R5.pin_0, R6.Pin_1
