# Fritzing sketch Voltage_Display (saved by Fritzing 0.9.3b)
breadboards: 1

parts:
  Part1 = Arduino Nano (Rev3.0)
  R1 = TRIMPOT [package=3386u]
  Grove1 = Grove OLED 128x96

nets:
  GND: Part1.GND, R1.CCW, Grove1.GND
  5V: Part1.5V, R1.CW, Grove1.VCC
  N1: Part1.A5, Grove1.SCL
  N2: Part1.A4, Grove1.SDA
  N3: Part1.A0, R1.WIPER
