# Fritzing sketch Voltage_serial (saved by Fritzing 0.9.3b)
breadboards: 1

parts:
  Part1 = Arduino Nano (Rev3.0)
  R1 = TRIMPOT [package=3386u]

nets:
  N1: Part1.GND, R1.CCW
  N2: Part1.5V, R1.CW
  N3: Part1.A0, R1.WIPER
