# Fritzing sketch ampel (saved by Fritzing 0.9.3b)
breadboards: 1

parts:
  Bauteil1 = Arduino Nano (Rev3.0) (ICSP)
  R1 = Resistor [tolerance=±5% resistance=220 package="2512 [SMD]"]
  LED2 = LED - 5mm [color="Yellow (595nm)" package="5 mm [THT]"]
  LED3 = LED - 5mm [color="Red (633nm)" package="5 mm [THT]"]
  LED4 = LED - 5mm [color="Green (555nm)" package="5 mm [THT]"]
  R2 = Resistor [tolerance=±5% resistance=220 package="2512 [SMD]"]
  R3 = Resistor [tolerance=±5% resistance=220 package="2512 [SMD]"]

nets:
  N1: Bauteil1.GND, LED2.cathode, LED3.cathode, LED4.cathode
  N2: Bauteil1.D2, R1.Pin_1
  N3: Bauteil1.D5, R2.Pin_1
  N4: Bauteil1.D12/MISO, R3.Pin_1
  N5: R1.Pin_0, LED3.anode
