# Fritzing sketch blink_extern (saved by Fritzing 0.9.3b)
breadboards: 1

parts:
  Bauteil1 = Arduino Nano (Rev3.0) (ICSP)
  R1 = Resistor [tolerance=±5% resistance=220 package="2512 [SMD]"]
  LED3 = LED - 5mm [color="Red (633nm)" package="5 mm [THT]"]

nets:
  N1: Bauteil1.GND, LED3.cathode
  N2: Bauteil1.D2, R1.Pin_1
  N3: R1.Pin_0, LED3.anode
